# Fritzing sketch Scheme (saved by Fritzing 0.9.3b)
breadboards: 3

parts:
  LCD1 = LCD screen
  Power_plug1 = Power plug
  KEYPAD1 = Membrane Matrix Keypad
  M4 = DC Motor
  R1 = Resistor [tolerance=±5% resistance=220 package=THT]
  Onderdeel1 = Arduino Mega ADK (Rev3)
  M7 = DC Motor
  M8 = DC Motor
  KY-5 = Keyes Relay [package=THT]
  KY-6 = Keyes Relay [package=THT]
  KY-7 = Keyes Relay [package=THT]
  KY-8 = Keyes Relay [package=THT]
  KY-9 = Keyes Relay [package=THT]
  M6 = DC Motor
  M5 = DC Motor
  KY-10 = Keyes Relay [package=THT]
  M9 = DC Motor
  KY-11 = Keyes Relay [package=THT]
  M10 = DC Motor
  KY-12 = Keyes Relay [package=THT]
  M11 = DC Motor
  KY-13 = Keyes Relay [package=THT]
  M12 = DC Motor
  microSD1 = MicroSD Card Module

nets:
  GND: LCD1.VSS, LCD1.V0, LCD1.R/W, LCD1.LED-, Onderdeel1.GND, KY-5.ground, KY-6.ground, KY-7.ground, KY-8.ground, KY-9.ground, KY-10.ground, KY-11.ground, KY-12.ground, KY-13.ground, microSD1.GND
  VDD: LCD1.VDD, R1.Pin_1, Onderdeel1.5V, KY-5.power, KY-6.power, KY-7.power, KY-8.power, KY-9.power, KY-10.power, KY-11.power, KY-12.power, KY-13.power, microSD1.VCC
  N1: LCD1.RS, Onderdeel1.D7_PWM
  N2: LCD1.E, Onderdeel1.D6_PWM
  N3: LCD1.DB4, Onderdeel1.D5_PWM
  N4: LCD1.DB5, Onderdeel1.D4_PWM
  N5: LCD1.DB6, Onderdeel1.D3_PWM
  N6: LCD1.DB7, Onderdeel1.D2_PWM
  N7: LCD1.LED+, R1.Pin_0
  N8: Power_plug1.GND, M4.pin_2, M7.pin_2, M8.pin_2, M6.pin_2, M5.pin_2, M9.pin_2, M10.pin_2, M11.pin_2, M12.pin_2
  N9: Power_plug1.VCC, KY-5.NO, KY-6.NO, KY-7.NO, KY-8.NO, KY-9.NO, KY-10.NO, KY-11.NO, KY-12.NO, KY-13.NO
  N10: KEYPAD1.1, Onderdeel1.D22
  N11: KEYPAD1.2, Onderdeel1.D24
  N12: KEYPAD1.3, Onderdeel1.D26
  N13: KEYPAD1.4, Onderdeel1.D28
  N14: KEYPAD1.5, Onderdeel1.D30
  N15: KEYPAD1.6, Onderdeel1.D32
  N16: KEYPAD1.7, Onderdeel1.D34
  N17: M4.pin_1, KY-9.C
  N18: Onderdeel1.D23, KY-13.signal
  N19: Onderdeel1.D25, KY-12.signal
  N20: Onderdeel1.D27, KY-11.signal
  N21: Onderdeel1.D29, KY-10.signal
  N22: Onderdeel1.D31, KY-9.signal
  N23: Onderdeel1.D33, KY-8.signal
  N24: Onderdeel1.D35, KY-7.signal
  N25: Onderdeel1.D37, KY-6.signal
  N26: Onderdeel1.D39, KY-5.signal
  N27: Onderdeel1.D50/MISO, microSD1.MISO
  N28: Onderdeel1.D51/MOSI, microSD1.MOSI
  N29: Onderdeel1.D52/SCK, microSD1.SCK
  N30: Onderdeel1.D53/SS, microSD1.CS
  N31: M7.pin_1, KY-5.C
  N32: M8.pin_1, KY-8.C
  N33: KY-6.C, M6.pin_1
  N34: KY-7.C, M5.pin_1
  N35: KY-10.C, M9.pin_1
  N36: KY-11.C, M10.pin_1
  N37: KY-12.C, M11.pin_1
  N38: KY-13.C, M12.pin_1

custom parts:
  Membrane Matrix Keypad: Membrane Matrix 3x4 Keypad
  Keyes Relay: The Keyes 5V relay module is suitable for SCM development, home appliance control. It uses a 5V~12V TIL control signal which can control DC / AC signal.
