# Fritzing sketch Scheme (saved by Fritzing 0.9.3b)
breadboards: 2

parts:
  LCD1 = LCD screen
  Power_plug1 = Power plug
  M1 = DC Motor
  KEYPAD1 = Membrane Matrix Keypad
  M2 = DC Motor
  M3 = DC Motor
  M4 = DC Motor
  R1 = Resistor [tolerance=±5% resistance=220 package=THT]
  8_Channel_Relay1 = 8 Channel Power Relay
  Onderdeel1 = Arduino Mega ADK (Rev3)
  M5 = DC Motor
  M6 = DC Motor
  M7 = DC Motor
  M8 = DC Motor

nets:
  GND: LCD1.VSS, LCD1.V0, LCD1.R/W, LCD1.LED-, 8_Channel_Relay1.GND, Onderdeel1.GND
  VDD: LCD1.VDD, R1.Pin_1, 8_Channel_Relay1.VCC, Onderdeel1.5V
  N1: LCD1.RS, Onderdeel1.D7_PWM
  N2: LCD1.E, Onderdeel1.D6_PWM
  N3: LCD1.DB4, Onderdeel1.D5_PWM
  N4: LCD1.DB5, Onderdeel1.D4_PWM
  N5: LCD1.DB6, Onderdeel1.D3_PWM
  N6: LCD1.DB7, Onderdeel1.D2_PWM
  N7: LCD1.LED+, R1.Pin_0
  N8: Power_plug1.GND, M1.pin_2, M2.pin_2, M3.pin_2, M4.pin_2, M5.pin_2, M6.pin_2, M7.pin_2, M8.pin_2
  N9: Power_plug1.VCC, 8_Channel_Relay1.COM
  N10: M1.pin_1, 8_Channel_Relay1.NC#21
  N11: KEYPAD1.1, Onderdeel1.D22
  N12: KEYPAD1.2, Onderdeel1.D24
  N13: KEYPAD1.3, Onderdeel1.D26
  N14: KEYPAD1.4, Onderdeel1.D28
  N15: KEYPAD1.5, Onderdeel1.D30
  N16: KEYPAD1.6, Onderdeel1.D32
  N17: KEYPAD1.7, Onderdeel1.D34
  N18: M2.pin_1, 8_Channel_Relay1.NC#24
  N19: M3.pin_1, 8_Channel_Relay1.NC#27
  N20: M4.pin_1, 8_Channel_Relay1.NC#30
  N21: 8_Channel_Relay1.IN1, Onderdeel1.D23
  N22: 8_Channel_Relay1.IN2, Onderdeel1.D25
  N23: 8_Channel_Relay1.IN3, Onderdeel1.D27
  N24: 8_Channel_Relay1.IN4, Onderdeel1.D29
  N25: 8_Channel_Relay1.IN5, Onderdeel1.D31
  N26: 8_Channel_Relay1.IN6, Onderdeel1.D33
  N27: 8_Channel_Relay1.IN7, Onderdeel1.D35
  N28: 8_Channel_Relay1.IN8, Onderdeel1.D37
  N29: 8_Channel_Relay1.NC#33, M8.pin_1
  N30: 8_Channel_Relay1.NC#36, M5.pin_1
  N31: 8_Channel_Relay1.NC#39, M6.pin_1
  N32: 8_Channel_Relay1.NC#42, M7.pin_1

custom parts:
  Membrane Matrix Keypad: Membrane Matrix 3x4 Keypad
  8 Channel Power Relay: An 8 channel power relay. The module operates at 5V.
